# Fritzing sketch GASSketch (saved by Fritzing 0.9.3b)

parts:
  Part1 = Arduino Uno (Rev3)
  J2 = Piezo Speaker
  Part2 = Gas Sensor Breakout Board
  F1 = Fan - Ventilador [package=THT]
  J3 = Basic Servo
  Part3 = Bluetooth HC-05 Macho

nets:
  N1: Part1.A0, Part2.A1
  N2: Part1.D8, J3.pulse
  N3: Part1.D9_PWM, F1.5V
  N4: Part1.D10_PWM/SS, Part3.TXD
  N5: Part1.D11_PWM/MOSI, Part3.RXD
  N6: Part1.D7, J2.pin2
  N7: Part1.5V, Part2.H1
  GND: Part1.GND, Part2.GND

custom parts:
  Fan - Ventilador: Ventilador de 2 pines, se encuentra comunmente en computadoras de escritorio
